// Logisim project s-mips.circ as structural Verilog: 22 circuits, main circuit S-MIPS Board
module S_MIPS_Board (
  input  DESHABILITAR_DISPATCHER,
  output halt
);

  wire button_1_out, CLK, CS, d_ff_1_q, LCLR, LoadRAM, LoadRAMOn, LW, R_R_W, R_W, ram_dispatcher_1_finished,
       RCS, Reset_out, RST, TTY_EN;
  wire [2:0] KDB;
  wire [3:0] LMask, Mask, ram_1_read_time, ram_1_write_time, RMask;
  wire [6:0] KDB_DATA, TTY_DATA;
  wire [15:0] Addr, LAddr, RAddr;
  wire [31:0] I0, I1, I2, I3, LData, ram_1_data_out_0, ram_1_data_out_1, ram_1_data_out_2, ram_1_data_out_3,
       RI0, RI1, RI2, RI3;

  TTY #(.rows(25), .cols(80)) tty_1 (.data(TTY_DATA), .clk(CLK), .we(TTY_EN), .clr(RST));
  not not_1 (LoadRAMOn, ram_dispatcher_1_finished);
  RAM_Dispatcher ram_dispatcher_1 (
    .WriteTime(ram_1_write_time), .Clock(CLK), .Data(LData), .Address(LAddr), .Mask(LMask),
    .Finished(ram_dispatcher_1_finished), .Write(LW), .CLR(LCLR));
  Keyboard #(.buflen(64)) keyboard_1 (.clk(CLK), .re(KDB[0]), .avail(KDB[2]), .data(KDB_DATA));  // open: clr
  RAM ram_1 (
    .Address(RAddr), .Data_Out_0(ram_1_data_out_0), .Data_Out_1(ram_1_data_out_1),
    .Data_Out_2(ram_1_data_out_2), .Data_Out_3(ram_1_data_out_3), .Data_In_0(RI0), .Data_In_1(RI1),
    .Data_In_2(RI2), .Data_In_3(RI3), .Mask(RMask), .nRead_Write(R_R_W), .Chip_Select(RCS),
    .Read_Time(ram_1_read_time), .Reset(button_1_out), .Write_Time(ram_1_write_time));
  Button button_1 (.out(button_1_out));
  D_Flip_Flop d_ff_1 (.clk(CLK), .D(1'b1), .Q(d_ff_1_q), .reset(Reset_out));  // open: Qn, preset, en
  Button Reset (.out(Reset_out));
  S_MIPS s_mips_1 (
    .Address(Addr), .Kbd_Available(KDB[2]), .RAM_In_0(I0), .Kbd_ASCII_Data(KDB_DATA), .RAM_In_1(I1),
    .TTY_Enable(TTY_EN), .RAM_In_2(I2), .RAM_In_3(I3), .TTY_ASCII_Data(TTY_DATA), .Reset(RST),
    .RAM_Out_0(ram_1_data_out_0), .Clock(CLK), .RAM_Out_1(ram_1_data_out_1), .Stop(halt),
    .RAM_Out_2(ram_1_data_out_2), .RAM_Out_3(ram_1_data_out_3), .Mask(Mask), .Read_Time(ram_1_read_time),
    .Write_Time(ram_1_write_time), .nRead_Write(R_W), .Chip_Select(CS), .Kbd_Enable(KDB[0]),
    .Kbd_Clear(KDB[1]));
  D_Flip_Flop d_ff_2 (.clk(CLK), .D(d_ff_1_q), .Qn(LCLR), .reset(Reset_out));  // open: Q, preset, en
  or or_1 (RST, LCLR, LoadRAM);
  Clock clock_1 (.out(CLK));
  Multiplexer #(.width(32), .enable("false")) multiplexer_1 (.in0(I0), .in1(LData), .out(RI0), .sel(LoadRAM));
  Multiplexer #(.width(32), .enable("false")) multiplexer_2 (.in0(I1), .in1(LData), .out(RI1), .sel(LoadRAM));
  Multiplexer #(.width(32), .enable("false")) multiplexer_3 (.in0(I2), .in1(LData), .out(RI2), .sel(LoadRAM));
  Multiplexer #(.width(32), .enable("false")) multiplexer_4 (.in0(I3), .in1(LData), .out(RI3), .sel(LoadRAM));
  and and_1 (LoadRAM, ~DESHABILITAR_DISPATCHER, LoadRAMOn);  // AND_Gate
  Multiplexer #(.width(16), .enable("false")) multiplexer_5 (.in0(Addr), .in1(LAddr), .out(RAddr), .sel(LoadRAM));
  Multiplexer #(.width(4), .enable("false")) multiplexer_6 (.in0(Mask), .in1(LMask), .out(RMask), .sel(LoadRAM));
  Multiplexer #(.enable("false")) multiplexer_7 (.in0(CS), .in1(LW), .out(RCS), .sel(LoadRAM));
  Multiplexer #(.enable("false")) multiplexer_8 (.in0(R_W), .in1(LW), .out(R_R_W), .sel(LoadRAM));

  // Notes on the sheet:
  //   NO MODIFICAR
  //   Keyboard
endmodule

module RAM (
  input  [15:0] Address,
  input  [31:0] Data_In_0,
  input  [31:0] Data_In_1,
  input  [31:0] Data_In_2,
  input  [31:0] Data_In_3,
  input  [3:0] Mask,
  input  nRead_Write,
  input  Chip_Select,
  input  Reset,
  output [31:0] Data_Out_0,
  output [31:0] Data_Out_1,
  output [31:0] Data_Out_2,
  output [31:0] Data_Out_3,
  output [3:0] Read_Time,
  output [3:0] Write_Time
);

  wire and_2_out, and_3_out, and_4_out, and_5_out, and_6_out, and_7_out, and_8_out, and_9_out, Changed, CLK,
       comparator_2_eq, comparator_3_eq, comparator_4_eq, comparator_5_eq, comparator_6_eq, Count,
       demultiplexer_3_out0, Idle, Idle_q, Load, Load0, Load1, nand_1_out, or_1_out, or_2_out, or_3_out,
       or_4_out, or_5_out, or_6_out, or_7_out, or_8_out, or_9_out, or_10_out, Proc_q, Update_Mem, Zero_Time;
  wire [3:0] counter_1_q, multiplexer_1_out, subtractor_1_out;
  wire [31:0] register_1_q, register_2_q, register_3_q, register_4_q, register_5_q;

  // Probe on 4'b0011
  // Probe on 4'b0010
  Multiplexer #(.width(4), .enable("false")) multiplexer_1 (
    .in0(4'b0011), .in1(4'b0010), .out(multiplexer_1_out), .sel(nRead_Write));
  or or_1 (or_1_out, Idle, Update_Mem);
  or or_2 (or_2_out, ~Chip_Select, Reset);  // OR_Gate
  Subtractor #(.width(4)) subtractor_1 (.a(multiplexer_1_out), .b(4'b0010), .out(subtractor_1_out));  // open: bin, bout
  Demultiplexer #(.enable("false")) demultiplexer_1 (.out0(Idle), .out1(Load0), .in(Idle_q), .sel(Changed));
  D_Flip_Flop u_Idle (.clk(CLK), .D(or_1_out), .Q(Idle_q), .preset(or_2_out));  // open: Qn, en, reset
  // Probe on counter_1_q
  Counter #(.width(4), .max('hf)) counter_1 (
    .load(Load), .D(subtractor_1_out), .count(Count), .Q(counter_1_q), .clk(CLK), .clr(or_3_out));  // open: carry
  or or_3 (or_3_out, ~Chip_Select, Reset);  // OR_Gate
  Comparator #(.width(4), .mode("unsigned")) comparator_1 (
    .a(4'b0000), .b(counter_1_q), .eq(Zero_Time));  // open: gt, lt
  or or_4 (or_4_out, Count, Load0, Load1);
  Register #(.width(32)) register_1 (.D(Data_In_0), .en(Chip_Select), .Q(register_1_q), .clk(CLK), .clr(or_5_out));
  or or_5 (or_5_out, ~Chip_Select, Reset);  // OR_Gate
  Register #(.width(32)) register_2 (.D(Data_In_1), .en(Chip_Select), .Q(register_2_q), .clk(CLK), .clr(or_6_out));
  or or_6 (or_6_out, ~Chip_Select, Reset);  // OR_Gate
  Register #(.width(32)) register_3 (.D(Data_In_2), .en(Chip_Select), .Q(register_3_q), .clk(CLK), .clr(or_7_out));
  or or_7 (or_7_out, ~Chip_Select, Reset);  // OR_Gate
  Register #(.width(32)) register_4 (.D(Data_In_3), .en(Chip_Select), .Q(register_4_q), .clk(CLK), .clr(or_8_out));
  or or_8 (or_8_out, ~Chip_Select, Reset);  // OR_Gate
  Register #(.width(32)) register_5 (
    .D({{11{1'b1}}, nRead_Write, Mask, Address}), .en(Chip_Select), .Q(register_5_q), .clk(CLK),
    .clr(or_9_out));
  or or_9 (or_9_out, ~Chip_Select, Reset);  // OR_Gate
  D_Flip_Flop Proc (.clk(CLK), .D(or_4_out), .Q(Proc_q), .reset(or_10_out));  // open: Qn, preset, en
  or or_10 (or_10_out, ~Chip_Select, Reset);  // OR_Gate
  Demultiplexer #(.enable("false")) demultiplexer_2 (
    .out0(Count), .out1(Update_Mem), .in(demultiplexer_3_out0), .sel(Zero_Time));
  Demultiplexer #(.enable("false")) demultiplexer_3 (
    .out0(demultiplexer_3_out0), .out1(Load1), .in(Proc_q), .sel(Changed));
  Clock clock_1 (.out(CLK));
  Comparator #(.width(32)) comparator_2 (.a(register_1_q), .b(Data_In_0), .eq(comparator_2_eq));  // open: gt, lt
  Comparator #(.width(32)) comparator_3 (.a(register_2_q), .b(Data_In_1), .eq(comparator_3_eq));  // open: gt, lt
  Comparator #(.width(32)) comparator_4 (.a(register_3_q), .b(Data_In_2), .eq(comparator_4_eq));  // open: gt, lt
  Comparator #(.width(32)) comparator_5 (.a(register_4_q), .b(Data_In_3), .eq(comparator_5_eq));  // open: gt, lt
  Comparator #(.width(32)) comparator_6 (
    .a(register_5_q), .b({{11{1'b1}}, nRead_Write, Mask, Address}), .eq(comparator_6_eq));  // open: gt, lt
  nand nand_1 (nand_1_out, comparator_6_eq, comparator_2_eq, comparator_3_eq, comparator_4_eq, comparator_5_eq);
  and and_1 (Changed, nand_1_out, Chip_Select);
  or or_11 (Load, Count, Load1, Load0);
  and and_2 (and_2_out, Mask[0], Update_Mem, nRead_Write);
  and and_3 (and_3_out, Mask[1], Update_Mem, nRead_Write);
  and and_4 (and_4_out, Mask[2], Update_Mem, nRead_Write);
  and and_5 (and_5_out, Mask[3], Update_Mem, nRead_Write);
  RAM_part #(.addrWidth(16), .dataWidth(32), .bus("separate")) ram_1 (
    .addr(Address), .din(Data_In_0), .data(Data_Out_0), .str(and_2_out), .sel(Chip_Select), .clk(CLK),
    .ld(and_6_out), .clr(Reset));
  and and_6 (and_6_out, ~nRead_Write, Idle);  // AND_Gate
  RAM_part #(.addrWidth(16), .dataWidth(32), .bus("separate")) ram_2 (
    .addr(Address), .din(Data_In_1), .data(Data_Out_1), .str(and_3_out), .sel(Chip_Select), .clk(CLK),
    .ld(and_7_out), .clr(Reset));
  and and_7 (and_7_out, ~nRead_Write, Idle);  // AND_Gate
  RAM_part #(.addrWidth(16), .dataWidth(32), .bus("separate")) ram_3 (
    .addr(Address), .din(Data_In_2), .data(Data_Out_2), .str(and_4_out), .sel(Chip_Select), .clk(CLK),
    .ld(and_8_out), .clr(Reset));
  and and_8 (and_8_out, ~nRead_Write, Idle);  // AND_Gate
  RAM_part #(.addrWidth(16), .dataWidth(32), .bus("separate")) ram_4 (
    .addr(Address), .din(Data_In_3), .data(Data_Out_3), .str(and_5_out), .sel(Chip_Select), .clk(CLK),
    .ld(and_9_out), .clr(Reset));
  and and_9 (and_9_out, ~nRead_Write, Idle);  // AND_Gate

  assign Read_Time = 4'b0011;
  assign Write_Time = 4'b0010;

  // Other names for the same wires on the sheet: M0 = Mask[0]; M1 = Mask[1]; M2 = Mask[2]; M3 = Mask[3];
  //   RW = nRead_Write; CLR = Reset; CS = Chip_Select; Load2 = Count

  // Notes on the sheet:
  //   NO MODIFICAR
  //   excepto quizás los valores RT y WT
  //   BANK0
  //   BANK1
  //   BANK2
  //   BANK3
endmodule

module RAM_Dispatcher (
  input  [3:0] WriteTime,
  input  Clock,
  input  CLR,
  output [31:0] Data,
  output [15:0] Address,
  output [3:0] Mask,
  output Finished,
  output Write
);

  wire demultiplexer_2_out1, demultiplexer_3_out1, End, IDLE_q, IncAddr, Load, or_1_out, or_2_out, While_q,
       WriteEnd;
  wire [3:0] counter_1_q;
  wire [31:0] CurrentAddress_q;

  Counter #(.width(32), .max('hffffffff)) CurrentAddress (
    .count(IncAddr), .Q({CurrentAddress_q[31:18], Address, CurrentAddress_q[1:0]}), .clk(Clock), .clr(CLR));  // open: load, D, carry
  or or_1 (or_1_out, IncAddr, demultiplexer_3_out1, Finished);
  D_Flip_Flop IDLE (.clk(Clock), .D(or_1_out), .Q(IDLE_q), .preset(CLR));  // open: Qn, en, reset
  Demultiplexer #(.enable("false")) demultiplexer_1 (.out0(Load), .out1(Finished), .in(IDLE_q), .sel(End));
  D_Flip_Flop While (.clk(Clock), .D(or_2_out), .Q(While_q), .reset(CLR));  // open: Qn, preset, en
  or or_2 (or_2_out, Write, Load);
  RAM_part #(.addrWidth(18), .dataWidth(32)) ram_1 (
    .addr({Address, CurrentAddress_q[1:0]}), .data(Data), .clk(Clock));  // open: sel, ld, clr
  Demultiplexer #(.enable("false")) demultiplexer_2 (
    .out0(Write), .out1(demultiplexer_2_out1), .in(While_q), .sel(WriteEnd));
  Decoder #(.select(2)) decoder_1 (
    .out0(Mask[0]), .out1(Mask[1]), .out2(Mask[2]), .out3(Mask[3]), .sel(CurrentAddress_q[1:0]));  // open: en
  Demultiplexer #(.enable("false")) demultiplexer_3 (
    .out0(IncAddr), .out1(demultiplexer_3_out1), .in(demultiplexer_2_out1), .sel(End));
  Counter #(.width(4), .max('hf)) counter_1 (
    .load(Load), .D(WriteTime), .count(Write), .Q(counter_1_q), .clk(Clock));  // open: carry, clr
  Comparator #(.width(32)) comparator_1 (.a(Data), .b({32{1'b1}}), .eq(End));  // open: gt, lt
  Comparator #(.width(4)) comparator_2 (.a(4'b0000), .b(counter_1_q), .eq(WriteEnd));  // open: gt, lt

  // Other names for the same wires on the sheet: CLK = Clock; Count = Write; WT[3:0] = WriteTime
endmodule

module S_MIPS (
  input  Kbd_Available,
  input  [31:0] RAM_Out_0,
  input  [6:0] Kbd_ASCII_Data,
  input  [31:0] RAM_Out_1,
  input  Reset,
  input  Clock,
  input  [31:0] RAM_Out_2,
  input  [3:0] Read_Time,
  input  [31:0] RAM_Out_3,
  input  [3:0] Write_Time,
  output [31:0] RAM_In_0,
  output Kbd_Enable,
  output TTY_Enable,
  output Kbd_Clear,
  output [6:0] TTY_ASCII_Data,
  output [31:0] RAM_In_1,
  output [3:0] Mask,
  output [15:0] Address,
  output [31:0] RAM_In_2,
  output nRead_Write,
  output Stop,
  output Chip_Select,
  output [31:0] RAM_In_3
);

  wire Cache_Hit, control_unit_1_e_id, control_unit_1_e_pc, E_Cache, Halt, R_IR, Read, Read_end, S_Src, src,
       w, Write_RAM;
  wire [31:0] Cache_Data, data_path_1_write_data, multiplexer_1_out, RAM_Adress, RAM_Data, Write_Data;

  Control_Unit control_unit_1 (
    .reset(Reset), .halt(Halt), .Read(Read), .Read_time(Read_Time), .Write_RAM(Write_RAM),
    .Write_time(Write_Time), .E_PC(control_unit_1_e_pc), .End(Stop), .E_ID(control_unit_1_e_id),
    .read_end(Read_end), .CS(Chip_Select), .R_W(nRead_Write), .clock(Clock), .R_IR(R_IR), .Stop_Src(S_Src),
    .Cache_Hit(Cache_Hit), .w(w), .src(src), .E_Cache(E_Cache));
  Read_Ram read_ram_1 (
    ._00(RAM_Out_0), ._01(RAM_Out_1), ._02(RAM_Out_2), ._03(RAM_Out_3), .Mem_Ram_Adress(RAM_Adress),
    .Read_Data(RAM_Data));
  Multiplexer #(.width(32), .enable("false")) multiplexer_1 (
    .in0(RAM_Data), .in1(Cache_Data), .out(multiplexer_1_out), .sel(Cache_Hit));
  // Probe on RAM_Data
  // Probe on Write_Data
  Data_Path data_path_1 (
    .keyboard(Kbd_ASCII_Data), .reset(Reset), .clock(Clock), .E_PC(control_unit_1_e_pc),
    .Instruction(multiplexer_1_out), .E_ID(control_unit_1_e_id), .kbd_A(Kbd_Available), .Read_RAM(Read_end),
    .TTY_Enable(TTY_Enable), .Kbd_Enable(Kbd_Enable), .halt(Halt), .WriteRAM(Write_RAM), .ReadRAM(Read),
    .RAM_Adress(RAM_Adress), .Write_Data(data_path_1_write_data), .tty_data(TTY_ASCII_Data), .R_IR(R_IR),
    .S_Src(S_Src), .w(w), .src(src));
  // Probe on RAM_Adress
  Write_Ram write_ram_1 (
    .Ram_Mem_Adress(RAM_Adress), .Mem_Write_Data(Write_Data), ._00(RAM_In_0), ._01(RAM_In_1), ._02(RAM_In_2),
    ._03(RAM_In_3), .mask(Mask), .RAM_A(Address));
  Cache cache_1 (
    .Mem_Adress(RAM_Adress), .WriteData(data_path_1_write_data), .Read(Read), .Write(Write_RAM),
    .Clock(Clock), .Reset(Reset), .Cache_Data(Write_Data), .Write_ram(Cache_Data), .Cache_Hit(Cache_Hit),
    .E_Cache(E_Cache), .Read_00(RAM_Out_0), .Read_01(RAM_Out_1), .Read_02(RAM_Out_2), .Read_03(RAM_Out_3));

  assign Kbd_Clear = Reset;

  // Other names for the same wires on the sheet: CLK = Clock; CLR = Reset; CS = Chip_Select;
  //   KBD_AVAIL = Kbd_Available; KBD_DATA[6:0] = Kbd_ASCII_Data; RAM_A[15:0] = Address; RAM_INPUT_0[31:0] = RAM_In_0;
  //   RAM_INPUT_1[31:0] = RAM_In_1; RAM_INPUT_2[31:0] = RAM_In_2; RAM_INPUT_3[31:0] = RAM_In_3; RAM_MASK[3:0] = Mask;
  //   RAM_OUTPUT_0[31:0] = RAM_Out_0; RAM_OUTPUT_1[31:0] = RAM_Out_1; RAM_OUTPUT_2[31:0] = RAM_Out_2;
  //   RAM_OUTPUT_3[31:0] = RAM_Out_3; RW = nRead_Write; TTY_DATA[6:0] = TTY_ASCII_Data

  // Notes on the sheet:
  //   DATA FROM RAM
  //   Inputs
  //   KEYBOARD
  //   SEQUENCING
  //   RAM TIMING
  //   Enable PC
  //   Enable ID
  //   DATA TO RAM
  //   Outputs
  //   TTY
  //   DATA WRITE MASK
  //   write
  //   read
  //   write data
  //   RAM CONTROL
  //   KEYBOARD
  //   RAM ADDRESS
endmodule

module Control_Unit (
  input  clock,
  input  Cache_Hit,
  input  reset,
  input  halt,
  input  Read,
  input  [3:0] Read_time,
  input  Write_RAM,
  input  [3:0] Write_time,
  input  src,
  output End,
  output R_W,
  output E_ID,
  output read_end,
  output E_PC,
  output CS,
  output R_IR,
  output Stop_Src,
  output w,
  output E_Cache
);

  wire c1, c2, Cache_q, demultiplexer_1_out1, demultiplexer_2_out0, demultiplexer_3_out0,
       demultiplexer_3_out1, demultiplexer_4_out0, demultiplexer_4_out1, demultiplexer_5_out0,
       demultiplexer_5_out1, demultiplexer_6_out1, demultiplexer_7_out0, demultiplexer_7_out1, Iddle_q,
       not_1_out, Operation_q, or_2_out, or_3_out, or_4_out, or_7_out, or_10_out, ram, rst_w, src_q, Timer;
  wire [3:0] counter_1_q, multiplexer_1_out, multiplexer_2_out;

  or or_1 (E_PC, w, demultiplexer_3_out0);
  or or_2 (or_2_out, demultiplexer_3_out0, w, demultiplexer_1_out1);
  Multiplexer #(.width(4), .enable("false")) multiplexer_1 (
    .in0(Read_time), .in1(Write_time), .out(multiplexer_1_out), .sel(Write_RAM));
  Demultiplexer #(.disabled(0), .enable("false")) demultiplexer_1 (
    .out0(R_IR), .out1(demultiplexer_1_out1), .in(Iddle_q), .sel(reset));
  D_Flip_Flop Iddle (.clk(clock), .D(or_2_out), .Q(Iddle_q), .preset(reset));  // open: Qn, en, reset
  Multiplexer #(.width(4), .enable("false")) multiplexer_2 (
    .in0(multiplexer_1_out), .in1(Read_time), .out(multiplexer_2_out), .sel(c1));
  or or_3 (or_3_out, demultiplexer_2_out0, R_IR);
  Comparator #(.width(4), .mode("unsigned")) comparator_1 (
    .a(multiplexer_2_out), .b(counter_1_q), .eq(Timer));  // open: gt, lt
  Counter #(.width(4), .max('hf)) counter_1 (
    .Q(counter_1_q), .clk(clock), .clr(or_4_out));  // open: load, D, count, carry
  or or_4 (or_4_out, R_IR, rst_w);
  D_Flip_Flop Fetch (.clk(clock), .D(or_3_out), .Q(c1), .reset(reset));  // open: Qn, preset, en
  Demultiplexer #(.disabled(0), .enable("false")) demultiplexer_2 (
    .out0(demultiplexer_2_out0), .out1(E_ID), .in(c1), .sel(Timer));
  D_Flip_Flop Operation (.clk(clock), .D(E_ID), .Q(Operation_q), .reset(reset));  // open: Qn, preset, en
  or or_5 (ram, Read, Write_RAM);
  or or_6 (CS, c1, c2);
  Demultiplexer #(.disabled(0), .enable("false")) demultiplexer_3 (
    .out0(demultiplexer_3_out0), .out1(demultiplexer_3_out1), .in(demultiplexer_4_out0), .sel(ram));
  Demultiplexer #(.enable("false")) demultiplexer_4 (
    .out0(demultiplexer_4_out0), .out1(demultiplexer_4_out1), .in(Operation_q), .sel(halt));
  Demultiplexer #(.disabled(0), .enable("false")) demultiplexer_5 (
    .out0(demultiplexer_5_out0), .out1(demultiplexer_5_out1), .in(demultiplexer_3_out1), .sel(not_1_out));
  or or_7 (or_7_out, demultiplexer_4_out1, End);
  D_Flip_Flop u_src (.clk(clock), .D(demultiplexer_5_out0), .Q(src_q), .reset(reset));  // open: Qn, preset, en
  not not_1 (not_1_out, src);
  D_Flip_Flop u_End (.clk(clock), .D(or_7_out), .Q(End), .reset(reset));  // open: Qn, preset, en
  and and_1 (R_W, c2, Write_RAM);
  or or_8 (Stop_Src, c2, rst_w, E_Cache, w, read_end);
  or or_9 (E_Cache, src_q, demultiplexer_5_out1);
  D_Flip_Flop Cache (.clk(clock), .D(E_Cache), .Q(Cache_q), .reset(reset));  // open: Qn, preset, en
  Demultiplexer #(.disabled(0), .enable("false")) demultiplexer_6 (
    .out0(rst_w), .out1(demultiplexer_6_out1), .in(Cache_q), .sel(Cache_Hit));
  or or_10 (or_10_out, demultiplexer_7_out0, rst_w);
  or or_11 (read_end, demultiplexer_6_out1, demultiplexer_7_out1);
  D_Flip_Flop u_R_W (.clk(clock), .D(or_10_out), .Q(c2), .reset(reset));  // open: Qn, preset, en
  D_Flip_Flop Wait (.clk(clock), .D(read_end), .Q(w), .reset(reset));  // open: Qn, preset, en
  Demultiplexer #(.enable("false")) demultiplexer_7 (
    .out0(demultiplexer_7_out0), .out1(demultiplexer_7_out1), .in(c2), .sel(Timer));

  // Other names for the same wires on the sheet: rst_r = R_IR

  // Notes on the sheet:
  //   Input
  //   Timer
  //   Control Unit
endmodule

module Data_Path (
  input  w,
  input  clock,
  input  Read_RAM,
  input  reset,
  input  S_Src,
  input  E_PC,
  input  [6:0] keyboard,
  input  E_ID,
  input  kbd_A,
  input  [31:0] Instruction,
  input  R_IR,
  output TTY_Enable,
  output [31:0] RAM_Adress,
  output Kbd_Enable,
  output halt,
  output src,
  output [31:0] Write_Data,
  output WriteRAM,
  output ReadRAM,
  output [6:0] tty_data
);

  wire B_Taken, beq, bgtz, blez, bltz, bne, is_ALU, is_LH, is_neg, is_zero, j, jr, logic_I, lw, mfhi, mflo,
       nop, pop, push, R, rnd, RW, sw, tty, type_I;
  wire [3:0] SEL;
  wire [4:0] multiplexer_2_out, Rd, Rs, Rt;
  wire [15:0] offset;
  wire [25:0] target;
  wire [31:0] A, B, bit_extender_1_out, bit_extender_2_out, constant, H, High, IR_q, L, multiplexer_3_out,
       Output, PCOut, rf_data_input_1_di, SP;

  or or_1 (R, R_IR, reset);
  BranchControl branchcontrol_1 (
    .beq(beq), .bne(bne), .blez(blez), .bgtz(bgtz), .bltz(bltz), .RD1(A), .RD2(B), .B_Taken(B_Taken));
  Program_Counter program_counter_1 (
    .Clock(clock), .Reset(reset), .Jump(j), .Jr(jr), .offset(offset), .target(target), .RsData(A),
    .PCWrite(E_PC), .BTaken(B_Taken), .PCOut(PCOut));
  Register #(.width(32)) IR (.D(Instruction), .en(E_ID), .Q(IR_q), .clk(clock), .clr(R));
  Instruction_Decoder instruction_decoder_1 (
    .Rs(Rs), .constant(offset), .Rt(Rt), .Rd(Rd), .target(target), .in_3(IR_q), .mfhi(mfhi), .halt(halt),
    .pop(pop), .mflo(mflo), .tty(tty), .push(push), .nop(nop), .rnd(rnd), .j(j), .jr(jr), .kbd(Kbd_Enable),
    .beq(beq), .bne(bne), .lw(lw), .blez(blez), .sw(sw), .bgtz(bgtz), .bltz(bltz), .logic_I(logic_I),
    .is_ALU(is_ALU), .is_LH(is_LH), .type_I(type_I), .SEL(SEL), .Read_RAM(Read_RAM), .RW(RW), .E_PC(E_PC));
  assign bit_extender_1_out = {{16{offset[15]}}, offset};  // Bit_Extender bit_extender_1
  assign bit_extender_2_out = {{16{1'b0}}, offset};  // Bit_Extender bit_extender_2
  Multiplexer #(.width(32), .enable("false")) multiplexer_1 (
    .in0(bit_extender_1_out), .in1(bit_extender_2_out), .out(constant), .sel(logic_I));
  Multiplexer #(.width(5), .enable("false")) multiplexer_2 (.in0(Rd), .in1(Rt), .out(multiplexer_2_out), .sel(type_I));
  and and_1 (TTY_Enable, E_PC, tty);
  RF_Data_Input rf_data_input_1 (
    .kbd(Kbd_Enable), .\rand (rnd), .mflo(mflo), .mfhi(mfhi), .lw(lw), .sw(sw), .ALU(Output),
    .DI(rf_data_input_1_di), .RAM(Instruction), .High(H), .Low(L), .clock(clock), .Kbd_2(keyboard),
    .E_kbd(kbd_A), .pop(pop), .reset(reset));
  Register_File register_file_1 (
    .RW(RW), .Clock(clock), .Reset(reset), .DI(rf_data_input_1_di), .A(A), .DataAdress(multiplexer_2_out),
    .SelectorA(Rs), .SelectorB(Rt), .Enable_High_Low(is_LH), .HighInput(High), .B(B), .SP(SP), .Low(L),
    .High(H), .push(push), .pop(pop), .Stop_Src(S_Src), .R_RAM(Read_RAM), .w(w));
  Multiplexer #(.width(32), .enable("false")) multiplexer_3 (
    .in0(B), .in1(constant), .out(multiplexer_3_out), .sel(type_I));
  ALU alu_1 (
    .in_1(A), .in_2(multiplexer_3_out), .in_3(SEL), .L(Output), .is_zero(is_zero), .is_negative(is_neg),
    .H(High));
  MemControl memcontrol_1 (
    .lw(lw), .sw(sw), .pop(pop), .push(push), .Rt_value(B), .Rs_value(A), .SM_Adress(SP), .offset(offset),
    .PCAdress(PCOut), .MemRead(ReadRAM), .MemWrite(WriteRAM), .RAM_Adress(RAM_Adress),
    .MemWrite_Data(Write_Data), .tty_data(tty_data));
  or or_2 (src, pop, push);

  // Other names for the same wires on the sheet: kbd = Kbd_Enable; R_RAM = Read_RAM; Read_data[31:0] = Instruction;
  //   WriteData[31:0] = Write_Data

  // Notes on the sheet:
  //   Input
  //   Data Path
  //   Output
endmodule

module Instruction_Decoder (
  input  Read_RAM,
  input  E_PC,
  input  [31:0] in_3,
  output [4:0] Rs,
  output [15:0] constant,
  output [4:0] Rt,
  output [4:0] Rd,
  output [25:0] target,
  output mfhi,
  output halt,
  output pop,
  output mflo,
  output tty,
  output push,
  output nop,
  output rnd,
  output j,
  output jr,
  output kbd,
  output beq,
  output bne,
  output lw,
  output blez,
  output sw,
  output bgtz,
  output bltz,
  output logic_I,
  output is_ALU,
  output is_LH,
  output type_I,
  output RW,
  output [3:0] SEL
);

  wire _000000, _111000, _111111, add, addi, ALU_type_I, \and , and_17_out, and_18_out, andi,
       comparator_6_eq, comparator_7_eq, comparator_8_eq, comparator_9_eq, comparator_10_eq,
       comparator_11_eq, comparator_12_eq, comparator_13_eq, comparator_23_eq, comparator_24_eq,
       comparator_25_eq, comparator_26_eq, comparator_27_eq, comparator_28_eq, comparator_29_eq,
       comparator_30_eq, comparator_32_eq, comparator_33_eq, comparator_34_eq, comparator_35_eq,
       comparator_37_eq, comparator_38_eq, div, divu, mult, mulu, \nor , \or , or_4_out, or_5_out, ori, slt,
       slti, sltiu, sltu, sub, \xor , xori;

  Comparator #(.width(6)) comparator_1 (.a(6'b000100), .b(in_3[31:26]), .eq(beq));  // open: gt, lt
  Comparator #(.width(6)) comparator_2 (.a(6'b000101), .b(in_3[31:26]), .eq(bne));  // open: gt, lt
  Comparator #(.width(6)) comparator_3 (.a(6'b000110), .b(in_3[31:26]), .eq(blez));  // open: gt, lt
  Comparator #(.width(6)) comparator_4 (.a(6'b000111), .b(in_3[31:26]), .eq(bgtz));  // open: gt, lt
  Comparator #(.width(6)) comparator_5 (.a(6'b000001), .b(in_3[31:26]), .eq(bltz));  // open: gt, lt
  and and_1 (add, _000000, comparator_6_eq);
  Comparator #(.width(6)) comparator_6 (.a(6'b100000), .b(in_3[5:0]), .eq(comparator_6_eq));  // open: gt, lt
  and and_2 (sub, _000000, comparator_7_eq);
  Comparator #(.width(6)) comparator_7 (.a(6'b100010), .b(in_3[5:0]), .eq(comparator_7_eq));  // open: gt, lt
  and and_3 (mult, _000000, comparator_8_eq);
  Comparator #(.width(6)) comparator_8 (.a(6'b011000), .b(in_3[5:0]), .eq(comparator_8_eq));  // open: gt, lt
  and and_4 (mulu, _000000, comparator_9_eq);
  Comparator #(.width(6)) comparator_9 (.a(6'b011001), .b(in_3[5:0]), .eq(comparator_9_eq));  // open: gt, lt
  ALU_Encoder alu_encoder_1 (
    .add(add), .addi(addi), .sub(sub), .slt(slt), .slti(slti), .sltu(sltu), .sltui(sltiu), .\and (\and ),
    .andi(andi), .\or (\or ), .ori(ori), .\xor (\xor ), .xori(xori), .\nor (\nor ), .mult(mult), .mulu(mulu),
    .div(div), .divu(divu), .Selector(SEL));
  Comparator #(.width(6)) comparator_10 (.a(6'b011010), .b(in_3[5:0]), .eq(comparator_10_eq));  // open: gt, lt
  Comparator #(.width(6)) comparator_11 (.a(6'b011011), .b(in_3[5:0]), .eq(comparator_11_eq));  // open: gt, lt
  Comparator #(.width(6)) comparator_12 (.a(6'b100100), .b(in_3[5:0]), .eq(comparator_12_eq));  // open: gt, lt
  Comparator #(.width(6)) comparator_13 (.a(6'b100101), .b(in_3[5:0]), .eq(comparator_13_eq));  // open: gt, lt
  Comparator #(.width(6)) comparator_14 (.a(6'b100011), .b(in_3[31:26]), .eq(lw));  // open: gt, lt
  Comparator #(.width(6)) comparator_15 (.a(6'b101011), .b(in_3[31:26]), .eq(sw));  // open: gt, lt
  Comparator #(.width(6)) comparator_16 (.a({6{1'b0}}), .b(in_3[31:26]), .eq(_000000));  // open: gt, lt
  and and_5 (div, _000000, comparator_10_eq);
  and and_6 (divu, _000000, comparator_11_eq);
  and and_7 (\and , _000000, comparator_12_eq);
  and and_8 (\or , _000000, comparator_13_eq);
  Comparator #(.width(6)) comparator_17 (.a(6'b001000), .b(in_3[31:26]), .eq(addi));  // open: gt, lt
  Comparator #(.width(6)) comparator_18 (.a(6'b001100), .b(in_3[31:26]), .eq(andi));  // open: gt, lt
  Comparator #(.width(6)) comparator_19 (.a(6'b001101), .b(in_3[31:26]), .eq(ori));  // open: gt, lt
  Comparator #(.width(6)) comparator_20 (.a(6'b001110), .b(in_3[31:26]), .eq(xori));  // open: gt, lt
  Comparator #(.width(6)) comparator_21 (.a(6'b001010), .b(in_3[31:26]), .eq(slti));  // open: gt, lt
  Comparator #(.width(6)) comparator_22 (.a(6'b001011), .b(in_3[31:26]), .eq(sltiu));  // open: gt, lt
  and and_9 (\nor , _000000, comparator_23_eq);
  Comparator #(.width(6)) comparator_23 (.a(6'b100111), .b(in_3[5:0]), .eq(comparator_23_eq));  // open: gt, lt
  and and_10 (\xor , _000000, comparator_24_eq);
  Comparator #(.width(6)) comparator_24 (.a(6'b101000), .b(in_3[5:0]), .eq(comparator_24_eq));  // open: gt, lt
  and and_11 (slt, _000000, comparator_25_eq);
  Comparator #(.width(6)) comparator_25 (.a(6'b101010), .b(in_3[5:0]), .eq(comparator_25_eq));  // open: gt, lt
  and and_12 (sltu, _000000, comparator_26_eq);
  Comparator #(.width(6)) comparator_26 (.a(6'b101011), .b(in_3[5:0]), .eq(comparator_26_eq));  // open: gt, lt
  Comparator #(.width(6)) comparator_27 (.a(6'b010000), .b(in_3[5:0]), .eq(comparator_27_eq));  // open: gt, lt
  Comparator #(.width(6)) comparator_28 (.a(6'b010010), .b(in_3[5:0]), .eq(comparator_28_eq));  // open: gt, lt
  Comparator #(.width(6)) comparator_29 (.a({6{1'b0}}), .b(in_3[5:0]), .eq(comparator_29_eq));  // open: gt, lt
  Comparator #(.width(6)) comparator_30 (.a(6'b001000), .b(in_3[5:0]), .eq(comparator_30_eq));  // open: gt, lt
  and and_13 (mfhi, _000000, comparator_27_eq);
  and and_14 (mflo, _000000, comparator_28_eq);
  and and_15 (nop, _000000, comparator_29_eq);
  and and_16 (jr, _000000, comparator_30_eq);
  or or_1 (is_LH, mult, mulu, div, divu);
  or or_2 (ALU_type_I, addi, andi, ori, xori, slti, sltiu);
  or or_3 (type_I, lw, sw, bltz, blez, beq, bne, bgtz, ALU_type_I);
  or or_4 (or_4_out, is_ALU, mfhi, mflo, kbd, rnd);
  or or_5 (or_5_out, pop, lw);
  Comparator #(.width(6)) comparator_31 (.a({6{1'b1}}), .b(in_3[31:26]), .eq(_111111));  // open: gt, lt
  Comparator #(.width(6)) comparator_32 (.a({6{1'b1}}), .b(in_3[5:0]), .eq(comparator_32_eq));  // open: gt, lt
  Comparator #(.width(6)) comparator_33 (.a(6'b000001), .b(in_3[5:0]), .eq(comparator_33_eq));  // open: gt, lt
  Comparator #(.width(6)) comparator_34 (.a(6'b000010), .b(in_3[5:0]), .eq(comparator_34_eq));  // open: gt, lt
  Comparator #(.width(6)) comparator_35 (.a(6'b000100), .b(in_3[5:0]), .eq(comparator_35_eq));  // open: gt, lt
  and and_17 (and_17_out, E_PC, or_4_out);
  and and_18 (and_18_out, or_5_out, Read_RAM);
  and and_19 (halt, _111111, comparator_32_eq);
  and and_20 (tty, _111111, comparator_33_eq);
  and and_21 (rnd, _111111, comparator_34_eq);
  and and_22 (kbd, _111111, comparator_35_eq);
  or or_6 (logic_I, andi, ori, xori);
  or or_7 (RW, and_17_out, and_18_out);
  or or_8 (is_ALU, add, sub, is_LH, \and , \or , \nor , \xor , slt, sltu, ALU_type_I);
  Comparator #(.width(6)) comparator_36 (.a(6'b111000), .b(in_3[31:26]), .eq(_111000));  // open: gt, lt
  Comparator #(.width(6)) comparator_37 (.a({6{1'b0}}), .b(in_3[5:0]), .eq(comparator_37_eq));  // open: gt, lt
  Comparator #(.width(6)) comparator_38 (.a(6'b000001), .b(in_3[5:0]), .eq(comparator_38_eq));  // open: gt, lt
  Comparator #(.width(6)) comparator_39 (.a(6'b000010), .b(in_3[31:26]), .eq(j));  // open: gt, lt
  and and_23 (pop, _111000, comparator_37_eq);
  and and_24 (push, _111000, comparator_38_eq);

  assign constant = in_3[15:0];
  assign Rd = in_3[15:11];
  assign Rs = in_3[25:21];
  assign Rt = in_3[20:16];
  assign target = in_3[25:0];

  // Other names for the same wires on the sheet: constat[15:0] = in_3[15:0]; func_code[5:0] = in_3[5:0];
  //   jump[25:0] = in_3[25:0]; x[4:0] = in_3[10:6]; op_code[5:0] = in_3[31:26]; Mult_or_Div = is_LH

  // Notes on the sheet:
  //   Instruction
  //   Instruction Decoder
  //   Type I
  //   Type R
  //   000000
  //   111111
  //   Type R
  //   Type R
  //   111000
  //   Type J
endmodule

module Register_File (
  input  RW,
  input  Clock,
  input  Reset,
  input  [31:0] DI,
  input  [4:0] DataAdress,
  input  [4:0] SelectorA,
  input  [4:0] SelectorB,
  input  Enable_High_Low,
  input  [31:0] HighInput,
  input  push,
  input  pop,
  input  Stop_Src,
  input  R_RAM,
  input  w,
  output [31:0] A,
  output [31:0] B,
  output [31:0] SP,
  output [31:0] Low,
  output [31:0] High
);

  wire and_1_out, and_2_out, not_1_out, or_1_out, SP_write, to0, to1, to2, to3, to4, to5, to6, to7, to8, to9,
       to10, to11, to12, to13, to14, to15, to16, to17, to18, to19, to20, to21, to22, to23, to24, to25, to26,
       to27, to28, to29, to30, to31;
  wire [31:0] multiplexer_1_out, multiplexer_2_out, output0, output1, output2, output3, output4, output5,
       output6, output7, output8, output9, output10, output11, output12, output13, output14, output15,
       output16, output17, output18, output19, output20, output21, output22, output23, output24, output25,
       output26, output27, output28, output29, output30, SP___4, SP___4_t, Stack_Adress;

  // Probe on DI
  Demultiplexer #(.select(5), .enable("false")) demultiplexer_1 (
    .out0(to0), .out1(to1), .out2(to2), .out3(to3), .out4(to4), .out5(to5), .out6(to6), .out7(to7),
    .out8(to8), .out9(to9), .out10(to10), .out11(to11), .out12(to12), .out13(to13), .out14(to14),
    .out15(to15), .out16(to16), .out17(to17), .out18(to18), .out19(to19), .out20(to20), .out21(to21),
    .out22(to22), .out23(to23), .out24(to24), .out25(to25), .out26(to26), .out27(to27), .out28(to28),
    .out29(to29), .out30(to30), .out31(to31), .in(RW), .sel(DataAdress));
  Register #(.width(32)) R0 (.D({32{1'b0}}), .en(to0), .Q(output0), .clk(Clock), .clr(Reset));
  Register #(.width(32)) R4 (.D(DI), .en(to4), .Q(output4), .clk(Clock), .clr(Reset));
  Register #(.width(32)) R8 (.D(DI), .en(to8), .Q(output8), .clk(Clock), .clr(Reset));
  Register #(.width(32)) R12 (.D(DI), .en(to12), .Q(output12), .clk(Clock), .clr(Reset));
  Register #(.width(32)) R16 (.D(DI), .en(to16), .Q(output16), .clk(Clock), .clr(Reset));
  Register #(.width(32)) R20 (.D(DI), .en(to20), .Q(output20), .clk(Clock), .clr(Reset));
  Register #(.width(32)) R24 (.D(DI), .en(to24), .Q(output24), .clk(Clock), .clr(Reset));
  Register #(.width(32)) R28 (.D(DI), .en(to28), .Q(output28), .clk(Clock), .clr(Reset));
  Register #(.width(32)) R1 (.D(DI), .en(to1), .Q(output1), .clk(Clock), .clr(Reset));
  Register #(.width(32)) R5 (.D(DI), .en(to5), .Q(output5), .clk(Clock), .clr(Reset));
  Register #(.width(32)) R9 (.D(DI), .en(to9), .Q(output9), .clk(Clock), .clr(Reset));
  Register #(.width(32)) R13 (.D(DI), .en(to13), .Q(output13), .clk(Clock), .clr(Reset));
  Register #(.width(32)) R17 (.D(DI), .en(to17), .Q(output17), .clk(Clock), .clr(Reset));
  Register #(.width(32)) R21 (.D(DI), .en(to21), .Q(output21), .clk(Clock), .clr(Reset));
  Register #(.width(32)) R25 (.D(DI), .en(to25), .Q(output25), .clk(Clock), .clr(Reset));
  Register #(.width(32)) R29 (.D(DI), .en(to29), .Q(output29), .clk(Clock), .clr(Reset));
  Register #(.width(32)) R2 (.D(DI), .en(to2), .Q(output2), .clk(Clock), .clr(Reset));
  Register #(.width(32)) R6 (.D(DI), .en(to6), .Q(output6), .clk(Clock), .clr(Reset));
  Register #(.width(32)) R10 (.D(DI), .en(to10), .Q(output10), .clk(Clock), .clr(Reset));
  Register #(.width(32)) R14 (.D(DI), .en(to14), .Q(output14), .clk(Clock), .clr(Reset));
  Register #(.width(32)) R18 (.D(DI), .en(to18), .Q(output18), .clk(Clock), .clr(Reset));
  Register #(.width(32)) R22 (.D(DI), .en(to22), .Q(output22), .clk(Clock), .clr(Reset));
  Register #(.width(32)) R26 (.D(DI), .en(to26), .Q(output26), .clk(Clock), .clr(Reset));
  Register #(.width(32)) R30 (.D(DI), .en(to30), .Q(output30), .clk(Clock), .clr(Reset));
  Register #(.width(32)) u_High (.D(HighInput), .en(Enable_High_Low), .Q(High), .clk(Clock), .clr(Reset));
  Multiplexer #(.width(32), .enable("false")) multiplexer_1 (
    .in0(SP), .in1(SP___4_t), .out(multiplexer_1_out), .sel(and_1_out));
  and and_1 (and_1_out, push, not_1_out);
  not not_1 (not_1_out, Stop_Src);
  Multiplexer #(.width(32), .enable("false")) multiplexer_2 (
    .in0(Stack_Adress), .in1(DI), .out(multiplexer_2_out), .sel(to31));
  or or_1 (or_1_out, to31, SP_write);
  and and_2 (and_2_out, w, pop);
  Register #(.width(32)) SP_R31 (.D(multiplexer_2_out), .en(or_1_out), .Q(SP), .clk(Clock), .clr(Reset));
  Register #(.width(32)) u_Low (.D(DI), .en(Enable_High_Low), .Q(Low), .clk(Clock), .clr(Reset));
  Multiplexer #(.width(32), .enable("false")) multiplexer_3 (
    .in0(multiplexer_1_out), .in1(SP___4), .out(Stack_Adress), .sel(and_2_out));
  Register #(.width(32)) R3 (.D(DI), .en(to3), .Q(output3), .clk(Clock), .clr(Reset));
  Register #(.width(32)) R7 (.D(DI), .en(to7), .Q(output7), .clk(Clock), .clr(Reset));
  Register #(.width(32)) R11 (.D(DI), .en(to11), .Q(output11), .clk(Clock), .clr(Reset));
  Register #(.width(32)) R15 (.D(DI), .en(to15), .Q(output15), .clk(Clock), .clr(Reset));
  Register #(.width(32)) R19 (.D(DI), .en(to19), .Q(output19), .clk(Clock), .clr(Reset));
  Register #(.width(32)) R23 (.D(DI), .en(to23), .Q(output23), .clk(Clock), .clr(Reset));
  Register #(.width(32)) R27 (.D(DI), .en(to27), .Q(output27), .clk(Clock), .clr(Reset));
  or or_2 (SP_write, pop, push);
  Adder #(.width(32)) adder_1 (.a(SP), .b(32'h4), .out(SP___4));  // open: cin, cout
  Subtractor #(.width(32)) subtractor_1 (.a(SP), .b(32'h4), .out(SP___4_t));  // open: bin, bout
  Multiplexer #(.select(5), .width(32), .enable("false")) multiplexer_4 (
    .in0(output0), .in1(output1), .in2(output2), .in3(output3), .in4(output4), .in5(output5), .in6(output6),
    .in7(output7), .in8(output8), .in9(output9), .in10(output10), .in11(output11), .in12(output12),
    .in13(output13), .in14(output14), .in15(output15), .in16(output16), .in17(output17), .in18(output18),
    .in19(output19), .in20(output20), .in21(output21), .in22(output22), .in23(output23), .in24(output24),
    .in25(output25), .in26(output26), .in27(output27), .in28(output28), .in29(output29), .in30(output30),
    .in31(SP), .out(A), .sel(SelectorA));
  Multiplexer #(.select(5), .width(32), .enable("false")) multiplexer_5 (
    .in0(output0), .in1(output1), .in2(output2), .in3(output3), .in4(output4), .in5(output5), .in6(output6),
    .in7(output7), .in8(output8), .in9(output9), .in10(output10), .in11(output11), .in12(output12),
    .in13(output13), .in14(output14), .in15(output15), .in16(output16), .in17(output17), .in18(output18),
    .in19(output19), .in20(output20), .in21(output21), .in22(output22), .in23(output23), .in24(output24),
    .in25(output25), .in26(output26), .in27(output27), .in28(output28), .in29(output29), .in30(output30),
    .in31(SP), .out(B), .sel(SelectorB));

  // Other names for the same wires on the sheet: Data_Input[31:0] = DI; E_HL = Enable_High_Low;
  //   High_Input[31:0] = HighInput; R_W = RW; SPoutput[31:0] = SP

  // Notes on the sheet:
  //   Register File
endmodule

module RF_Data_Input (
  input  kbd,
  input  \rand ,
  input  mflo,
  input  mfhi,
  input  lw,
  input  sw,
  input  clock,
  input  E_kbd,
  input  pop,
  input  reset,
  input  [31:0] ALU,
  input  [31:0] High,
  input  [31:0] RAM,
  input  [31:0] Low,
  input  [6:0] Kbd_2,
  output [31:0] DI
);

  wire ram_t;
  wire [2:0] or_2_out;
  wire [31:0] KBD_t, keyboard, random;

  assign keyboard = {{25{1'b0}}, Kbd_2};  // Bit_Extender bit_extender_1
  Random #(.width(32)) random_1 (.clk(clock), .next(\rand ), .out(random));  // open: clr
  Multiplexer #(.width(32), .enable("false")) multiplexer_1 (
    .in0({32{1'b1}}), .in1(keyboard), .out(KBD_t), .sel(E_kbd));
  or or_1 (ram_t, lw, pop);
  or or_2 (or_2_out[0], kbd, ram_t, mflo);
  or or_3 (or_2_out[1], \rand , ram_t);
  or or_4 (or_2_out[2], mfhi, mflo);
  Multiplexer #(.select(3), .width(32), .disabled(0), .enable("false")) multiplexer_2 (
    .in0(ALU), .in1(KBD_t), .in2(random), .in3(RAM), .in4(High), .in5(Low), .out(DI), .sel(or_2_out));  // open: in6, in7
  // Probe on or_2_out
endmodule

module ALU (
  input  [31:0] in_1,
  input  [31:0] in_2,
  input  [3:0] in_3,
  output [31:0] L,
  output is_zero,
  output is_negative,
  output [31:0] H
);

  wire comparator_1_lt, comparator_2_lt;
  wire [31:0] add, \and , div, div_H, divu, divu_H, mult, mult_H, multiplexer_2_out, mulu, mulu_H, \nor ,
       \or , slt, sltu, sub, \xor ;

  Adder #(.width(32)) adder_1 (.a(in_1), .b(in_2), .out(add));  // open: cin, cout
  Subtractor #(.width(32)) subtractor_1 (.a(in_1), .b(in_2), .out(sub));  // open: bin, bout
  Comparator #(.width(32)) comparator_1 (.a(in_1), .b(in_2), .lt(comparator_1_lt));  // open: gt, eq
  Comparator #(.width(32), .mode("unsigned")) comparator_2 (.a(in_1), .b(in_2), .lt(comparator_2_lt));  // open: gt, eq
  // Probe on in_1
  // Probe on in_2
  // Probe on in_3
  assign slt = {{31{1'b0}}, comparator_1_lt};  // Bit_Extender bit_extender_1
  assign sltu = {{31{1'b0}}, comparator_2_lt};  // Bit_Extender bit_extender_2
  assign \and  = in_1 & in_2;  // AND_Gate and_1, 32 bits wide
  assign \or  = in_1 | in_2;  // OR_Gate or_1, 32 bits wide
  assign \nor  = ~(in_1 | in_2);  // NOR_Gate nor_1, 32 bits wide
  assign \xor  = in_1 ^ in_2;  // XOR_Gate xor_1, 32 bits wide
  Multiplexer #(.select(4), .width(32), .enable("false")) multiplexer_1 (
    .in0(add), .in1(sub), .in2(slt), .in3(sltu), .in4(\and ), .in5(\or ), .in6(\xor ), .in7(\nor ),
    .in8(mult), .in9(mulu), .in10(div), .in11(divu), .in12({32{1'b0}}), .in13({32{1'b0}}), .in14({32{1'b0}}),
    .in15({32{1'b0}}), .out(L), .sel(in_3));
  // Probe on L
  Signed_Div signed_div_1 (.A(in_1), .B(in_2), .out_3(div), .out_4(div_H));
  Divider #(.width(32)) divider_1 (.a(in_1), .b(in_2), .out(divu), .rem(divu_H));  // open: upper
  Comparator #(.width(32)) comparator_3 (.a(L), .b({32{1'b0}}), .eq(is_zero), .lt(is_negative));  // open: gt
  Multiplexer #(.select(2), .width(32), .enable("false")) multiplexer_2 (
    .in0(mult_H), .in1(mulu_H), .in2(div_H), .in3(divu_H), .out(multiplexer_2_out), .sel(in_3[1:0]));
  Multiplexer #(.width(32), .enable("false")) multiplexer_3 (
    .in0({32{1'b0}}), .in1(multiplexer_2_out), .out(H), .sel(in_3[3]));
  Signed_Mult signed_mult_1 (.A(in_1), .B(in_2), .out_3(mult), .out_4(mult_H));
  Multiplier #(.width(32)) multiplier_1 (.a(in_1), .b(in_2), .out(mulu), .cout(mulu_H));  // open: cin

  // Other names for the same wires on the sheet: A[31:0] = in_1; B[31:0] = in_2; Function[1:0] = in_3[1:0];
  //   SEL[3:0] = in_3; Mult_or_Div = in_3[3]

  // Notes on the sheet:
  //   Aritmetic Logic Unit
  //   Input
  //   Selector
  //   Functions
  //   0000
  //   0001
  //   0010
  //   0011
  //   0100
  //   0101
  //   0110
  //   0111
  //   1000
  //   1001
  //   1010
  //   1011
  //   1100
  //   1101
  //   1110
  //   1111
  //   Output
  //   High
  //   Output
endmodule

module ALU_Encoder (
  input  add,
  input  addi,
  input  sub,
  input  slt,
  input  slti,
  input  sltu,
  input  sltui,
  input  \and ,
  input  andi,
  input  \or ,
  input  ori,
  input  \xor ,
  input  xori,
  input  \nor ,
  input  mult,
  input  mulu,
  input  div,
  input  divu,
  output [3:0] Selector
);

  wire add_t, and_t, or_t, slt_t, sltu_t, xor_t;

  or or_1 (add_t, add, addi);
  or or_2 (slt_t, slt, slti);
  or or_3 (sltu_t, sltu, sltui);
  or or_4 (and_t, \and , andi);
  or or_5 (or_t, \or , ori);
  or or_6 (xor_t, \xor , xori);
  or or_7 (Selector[0], sub, sltu_t, or_t, \nor , mulu, divu);
  or or_8 (Selector[1], slt_t, sltu_t, xor_t, \nor , div, divu);
  or or_9 (Selector[2], and_t, or_t, xor_t, \nor );
  or or_10 (Selector[3], mult, mulu, div, divu);

  // Other names for the same wires on the sheet: bit_0 = Selector[0]; bit_1 = Selector[1]; bit_2 = Selector[2];
  //   bit_3 = Selector[3]

  // Notes on the sheet:
  //   Input
  //   ALU ENCODER
  //   Output
endmodule

module Signed_Mult (
  input  [31:0] A,
  input  [31:0] B,
  output [31:0] out_3,
  output [31:0] out_4
);

  wire xor_1_out;
  wire [31:0] multiplexer_1_out, multiplexer_2_out, multiplier_1_out, negator_1_out, negator_2_out,
       negator_3_out;

  // Probe on A
  // Probe on B
  Negator #(.width(32)) negator_1 (.in(A), .out(negator_1_out));
  Negator #(.width(32)) negator_2 (.in(B), .out(negator_2_out));
  Multiplexer #(.width(32), .enable("false")) multiplexer_1 (
    .in0(A), .in1(negator_1_out), .out(multiplexer_1_out), .sel(A[31]));
  Multiplexer #(.width(32), .enable("false")) multiplexer_2 (
    .in0(B), .in1(negator_2_out), .out(multiplexer_2_out), .sel(B[31]));
  Multiplier #(.width(32)) multiplier_1 (
    .a(multiplexer_1_out), .b(multiplexer_2_out), .out(multiplier_1_out), .cout(out_4));  // open: cin
  Negator #(.width(32)) negator_3 (.in(multiplier_1_out), .out(negator_3_out));
  xor xor_1 (xor_1_out, A[31], B[31]);
  // Probe on out_3
  Multiplexer #(.width(32), .enable("false")) multiplexer_3 (
    .in0(multiplier_1_out), .in1(negator_3_out), .out(out_3), .sel(xor_1_out));
  // Probe on out_4

  // Other names for the same wires on the sheet: Sel_A = A[31]; Sel_B = B[31]

  // Notes on the sheet:
  //   Input
  //   Output
  //   Carry Out
endmodule

module Signed_Div (
  input  [31:0] A,
  input  [31:0] B,
  output [31:0] out_3,
  output [31:0] out_4
);

  wire xor_1_out, xor_2_out;
  wire [31:0] divider_1_out, divider_1_rem, multiplexer_1_out, multiplexer_2_out, negator_1_out,
       negator_2_out, negator_3_out, negator_4_out;

  // Probe on A
  // Probe on B
  Negator #(.width(32)) negator_1 (.in(A), .out(negator_1_out));
  Negator #(.width(32)) negator_2 (.in(B), .out(negator_2_out));
  Multiplexer #(.width(32), .enable("false")) multiplexer_1 (
    .in0(A), .in1(negator_1_out), .out(multiplexer_1_out), .sel(A[31]));
  Multiplexer #(.width(32), .enable("false")) multiplexer_2 (
    .in0(B), .in1(negator_2_out), .out(multiplexer_2_out), .sel(B[31]));
  Divider #(.width(32)) divider_1 (
    .a(multiplexer_1_out), .b(multiplexer_2_out), .out(divider_1_out), .rem(divider_1_rem));  // open: upper
  Negator #(.width(32)) negator_3 (.in(divider_1_out), .out(negator_3_out));
  xor xor_1 (xor_1_out, A[31], B[31]);
  Negator #(.width(32)) negator_4 (.in(divider_1_rem), .out(negator_4_out));
  xor xor_2 (xor_2_out, A[31], B[31]);
  // Probe on out_3
  Multiplexer #(.width(32), .enable("false")) multiplexer_3 (
    .in0(divider_1_out), .in1(negator_3_out), .out(out_3), .sel(xor_1_out));
  Multiplexer #(.width(32), .enable("false")) multiplexer_4 (
    .in0(divider_1_rem), .in1(negator_4_out), .out(out_4), .sel(xor_2_out));
  // Probe on out_4

  // Other names for the same wires on the sheet: Sel_A = A[31]; Sel_B = B[31]

  // Notes on the sheet:
  //   Input
  //   Output
  //   Rest
endmodule

module Program_Counter (
  input  Clock,
  input  Reset,
  input  Jump,
  input  Jr,
  input  [15:0] offset,
  input  [25:0] target,
  input  [31:0] RsData,
  input  PCWrite,
  input  BTaken,
  output [31:0] PCOut
);

  wire and_2_out, not_1_out;
  wire [25:0] shifter_2_out;
  wire [31:0] bit_extender_1_out, Branch_Adress, Jump_Adress, Output, PC_High, PCNext_Branch, PCplus4,
       shifter_1_out, TargetShifted;

  assign bit_extender_1_out = {{16{offset[15]}}, offset};  // Bit_Extender bit_extender_1
  Adder #(.width(32)) adder_1 (.a(PCOut), .b(32'h4), .out(PCplus4));  // open: cin, cout
  Multiplexer #(.width(32), .enable("false")) multiplexer_1 (
    .in0(PCplus4), .in1(Branch_Adress), .out(PCNext_Branch), .sel(BTaken));
  Shifter #(.width(32)) shifter_1 (.in(bit_extender_1_out), .\dist (5'b00010), .out(shifter_1_out));
  assign PC_High = PCplus4 & 32'hf0000000;  // AND_Gate and_1, 32 bits wide
  assign TargetShifted = {{6{1'b0}}, shifter_2_out};  // Bit_Extender bit_extender_2
  Shifter #(.width(26)) shifter_2 (.in(target), .\dist (5'b00010), .out(shifter_2_out));
  Adder #(.width(32)) adder_2 (.a(PCplus4), .b(shifter_1_out), .out(Branch_Adress));  // open: cin, cout
  assign Jump_Adress = PC_High | TargetShifted;  // OR_Gate or_1, 32 bits wide
  and and_2 (and_2_out, PCWrite, not_1_out);
  not not_1 (not_1_out, Reset);
  Multiplexer #(.select(2), .width(32), .enable("false")) multiplexer_2 (
    .in0(PCNext_Branch), .in1(Jump_Adress), .in2(RsData), .in3({32{1'b0}}), .out(Output), .sel({Jr, Jump}));
  Register #(.width(32)) PC (.D(Output), .en(and_2_out), .Q(PCOut), .clk(Clock), .clr(Reset));

  // Other names for the same wires on the sheet: BranchTaken = BTaken

  // Notes on the sheet:
  //   Program Counter
endmodule

module BranchControl (
  input  beq,
  input  bne,
  input  blez,
  input  bgtz,
  input  bltz,
  input  [31:0] RD1,
  input  [31:0] RD2,
  output B_Taken
);

  wire and_2_out, and_6_out, areEqual, beq_taken, bgtz_taken, blez_taken, bltz_taken, bne_taken, isZero,
       not_1_out, not_2_out, not_3_out, not_4_out, or_1_out;

  and and_1 (beq_taken, beq, areEqual);
  not not_1 (not_1_out, areEqual);
  or or_1 (or_1_out, RD1[31], isZero);
  and and_2 (and_2_out, RD1[31], not_2_out);
  not not_2 (not_2_out, isZero);
  Comparator #(.width(32)) comparator_1 (.a(RD1), .b({32{1'b0}}), .eq(isZero));  // open: gt, lt
  and and_3 (bne_taken, bne, not_1_out);
  and and_4 (blez_taken, blez, or_1_out);
  not not_3 (not_3_out, RD1[31]);
  not not_4 (not_4_out, isZero);
  and and_5 (bltz_taken, and_2_out, bltz);
  and and_6 (and_6_out, not_3_out, not_4_out);
  Comparator #(.width(32)) comparator_2 (.a(RD1), .b(RD2), .eq(areEqual));  // open: gt, lt
  and and_7 (bgtz_taken, and_6_out, bgtz);
  or or_2 (B_Taken, beq_taken, bne_taken, blez_taken, bgtz_taken, bltz_taken);

  // Other names for the same wires on the sheet: ReadData1[31:0] = RD1; sign = RD1[31]; ReadData2[31:0] = RD2

  // Notes on the sheet:
  //   Branch Control
endmodule

module MemControl (
  input  lw,
  input  sw,
  input  pop,
  input  push,
  input  [31:0] Rs_value,
  input  [31:0] Rt_value,
  input  [15:0] offset,
  input  [31:0] SM_Adress,
  input  [31:0] PCAdress,
  output MemRead,
  output MemWrite,
  output [31:0] RAM_Adress,
  output [31:0] MemWrite_Data,
  output [6:0] tty_data
);

  wire Is_DataIn, MemSrc;
  wire [31:0] bit_extender_1_out, Result;

  or or_1 (MemSrc, pop, push);
  assign bit_extender_1_out = {{16{offset[15]}}, offset};  // Bit_Extender bit_extender_1
  Multiplexer #(.width(32), .enable("false")) multiplexer_1 (
    .in0(Rt_value), .in1(Rs_value), .out(MemWrite_Data), .sel(MemSrc));
  Adder #(.width(32)) adder_1 (.a(bit_extender_1_out), .b(Rs_value), .out(Result));  // open: cin, cout
  Multiplexer #(.select(2), .width(32), .enable("false")) multiplexer_2 (
    .in0(PCAdress), .in1(Result), .in2(SM_Adress), .in3({32{1'b0}}), .out(RAM_Adress),
    .sel({MemSrc, Is_DataIn}));
  or or_2 (Is_DataIn, lw, sw);
  or or_3 (MemRead, pop, lw);
  or or_4 (MemWrite, push, sw);

  assign tty_data = Rs_value[6:0];

  // Other names for the same wires on the sheet: MemWriteData[31:0] = MemWrite_Data; PC_Adress[31:0] = PCAdress;
  //   RAM_Mem_Adress[31:0] = RAM_Adress; SP[31:0] = SM_Adress

  // Notes on the sheet:
  //   Mem Control
endmodule

module Little_Endian (
  input  [31:0] in_1,
  output [31:0] out_2
);


  assign out_2 = {in_1[7:0], in_1[15:8], in_1[23:16], in_1[31:24]};

  // Notes on the sheet:
  //   Input
  //   LITTLE ENDIAN - BIG ENDIAN
  //   Output
endmodule

module Read_Ram (
  input  [31:0] _00,
  input  [31:0] _01,
  input  [31:0] _02,
  input  [31:0] Mem_Ram_Adress,
  input  [31:0] _03,
  output [31:0] Read_Data
);

  wire [31:0] multiplexer_1_out;

  Multiplexer #(.select(2), .width(32), .enable("false")) multiplexer_1 (
    .in0(_00), .in1(_01), .in2(_02), .in3(_03), .out(multiplexer_1_out), .sel(Mem_Ram_Adress[3:2]));
  Little_Endian little_endian_1 (.in_1(multiplexer_1_out), .out_2(Read_Data));

  // Other names for the same wires on the sheet: Bank0[31:0] = _00; Bank1[31:0] = _01; Bank2[31:0] = _02;
  //   Bank3[31:0] = _03; Low_mem[1:0] = Mem_Ram_Adress[3:2]
endmodule

module Write_Ram (
  input  [31:0] Ram_Mem_Adress,
  input  [31:0] Mem_Write_Data,
  output [31:0] _00,
  output [31:0] _01,
  output [31:0] _02,
  output [31:0] _03,
  output [3:0] mask,
  output [15:0] RAM_A
);

  wire [31:0] little_endian_1_out_2;

  Multiplexer #(.select(2), .width(4), .enable("false")) multiplexer_1 (
    .in0(4'b0001), .in1(4'b0010), .in2(4'b0100), .in3(4'b1000), .out(mask), .sel(Ram_Mem_Adress[3:2]));
  Little_Endian little_endian_1 (.in_1(Mem_Write_Data), .out_2(little_endian_1_out_2));
  Demultiplexer #(.select(2), .width(32), .enable("false")) demultiplexer_1 (
    .out0(_00), .out1(_01), .out2(_02), .out3(_03), .in(little_endian_1_out_2), .sel(Ram_Mem_Adress[3:2]));

  assign RAM_A = Ram_Mem_Adress[19:4];

  // Other names for the same wires on the sheet: Mem_Adress_low[1:0] = Ram_Mem_Adress[3:2]
endmodule

module Cache (
  input  Clock,
  input  Reset,
  input  Read,
  input  Write,
  input  E_Cache,
  input  [31:0] Mem_Adress,
  input  [31:0] WriteData,
  input  [31:0] Read_00,
  input  [31:0] Read_01,
  input  [31:0] Read_02,
  input  [31:0] Read_03,
  output Cache_Hit,
  output [31:0] Write_ram,
  output [31:0] Cache_Data
);

  wire _0_enable, _1_enable, _2_enable, _3_enable, and_2_out, and_5_out, and_6_out, and_7_out, and_8_out,
       and_9_out, and_10_out, and_11_out, and_12_out, and_13_out, and_14_out, and_15_out, and_16_out,
       and_17_out, and_18_out, and_19_out, and_20_out, and_29_out, and_30_out, and_31_out, and_32_out,
       and_33_out, and_34_out, and_35_out, and_36_out, and_37_out, and_38_out, and_39_out, and_40_out,
       and_45_out, and_47_out, and_49_out, and_51_out, bank0, bank1, bank2, bank3, Cache_Hit_t, Cache_in,
       E00, E01, E02, E03, E10, E11, E12, E13, E20, E21, E22, E23, E30, E31, E32, E33, Line1_Enable,
       Line2_Enable, Line3_Enable, Line4_Enable, Line_Enable, not_1_out, not_2_out, not_3_out, Ram_Read,
       Tags_Same;
  wire [14:0] Selected_Tag_Valid, V_Tag1, V_Tag2, V_Tag3, V_Tag4;
  wire [31:0] L1_Banco00, L1_Banco01, L1_Banco02, L1_Banco03, L2_Banco00, L2_Banco01, L2_Banco02, L2_Banco03,
       L3_Banco00, L3_Banco01, L3_Banco02, L3_Banco03, L4_Banco00, L4_Banco01, L4_Banco02, L4_Banco03,
       little_endian_1_out_2, little_endian_2_out_2, little_endian_3_out_2, little_endian_4_out_2, Read_00_t,
       Read_01_t, Read_02_t, Read_03_t, Selected_BankL1, Selected_BankL2, Selected_BankL3, Selected_BankL4;

  Multiplexer #(.select(2), .width(15), .enable("false")) multiplexer_1 (
    .in0(V_Tag1), .in1(V_Tag2), .in2(V_Tag3), .in3(V_Tag4), .out(Selected_Tag_Valid), .sel(Mem_Adress[5:4]));
  Little_Endian little_endian_1 (.in_1(Read_00), .out_2(little_endian_1_out_2));
  Little_Endian little_endian_2 (.in_1(Read_01), .out_2(little_endian_2_out_2));
  Little_Endian little_endian_3 (.in_1(Read_02), .out_2(little_endian_3_out_2));
  Little_Endian little_endian_4 (.in_1(Read_03), .out_2(little_endian_4_out_2));
  Multiplexer #(.width(32), .enable("false")) multiplexer_2 (
    .in0(WriteData), .in1(little_endian_1_out_2), .out(Read_00_t), .sel(not_1_out));
  not not_1 (not_1_out, bank0);
  Multiplexer #(.width(32), .enable("false")) multiplexer_3 (
    .in0(little_endian_2_out_2), .in1(WriteData), .out(Read_01_t), .sel(bank1));
  Multiplexer #(.width(32), .enable("false")) multiplexer_4 (
    .in0(little_endian_3_out_2), .in1(WriteData), .out(Read_02_t), .sel(bank2));
  Multiplexer #(.width(32), .enable("false")) multiplexer_5 (
    .in0(little_endian_4_out_2), .in1(WriteData), .out(Read_03_t), .sel(bank2));
  or or_1 (Cache_in, Read, Write);
  and and_1 (Line_Enable, Write, not_2_out);
  not not_2 (not_2_out, Cache_Hit_t);
  and and_2 (and_2_out, Line_Enable, E_Cache);
  Demultiplexer #(.select(2), .enable("false")) demultiplexer_1 (
    .out0(Line1_Enable), .out1(Line2_Enable), .out2(Line3_Enable), .out3(Line4_Enable), .in(and_2_out),
    .sel(Mem_Adress[5:4]));
  Register #(.width(15)) u_V_Tag1 (
    .D({1'b1, Mem_Adress[19:6]}), .en(Line1_Enable), .Q(V_Tag1), .clk(Clock), .clr(Reset));
  Register #(.width(15)) u_V_Tag2 (
    .D({1'b1, Mem_Adress[19:6]}), .en(Line2_Enable), .Q(V_Tag2), .clk(Clock), .clr(Reset));
  Register #(.width(15)) V_Tag2_2 (
    .D({1'b1, Mem_Adress[19:6]}), .en(Line3_Enable), .Q(V_Tag3), .clk(Clock), .clr(Reset));
  Register #(.width(15)) u_V_Tag4 (
    .D({1'b1, Mem_Adress[19:6]}), .en(Line4_Enable), .Q(V_Tag4), .clk(Clock), .clr(Reset));
  Multiplexer #(.select(2), .width(32), .enable("false")) multiplexer_6 (
    .in0(L1_Banco00), .in1(L1_Banco01), .in2(L1_Banco02), .in3(L1_Banco03), .out(Selected_BankL1),
    .sel(Mem_Adress[3:2]));
  Multiplexer #(.select(2), .width(32), .enable("false")) multiplexer_7 (
    .in0(L3_Banco00), .in1(L3_Banco01), .in2(L3_Banco02), .in3(L3_Banco03), .out(Selected_BankL3),
    .sel(Mem_Adress[3:2]));
  Register #(.width(32)) u_L1_Banco00 (.D(Read_00_t), .en(Line1_Enable), .Q(L1_Banco00), .clk(Clock), .clr(Reset));
  Register #(.width(32)) u_L2_Banco00 (.D(Read_00_t), .en(Line2_Enable), .Q(L2_Banco00), .clk(Clock), .clr(Reset));
  Register #(.width(32)) u_L3_Banco00 (.D(Read_00_t), .en(Line3_Enable), .Q(L3_Banco00), .clk(Clock), .clr(Reset));
  Register #(.width(32)) u_L4_Banco00 (.D(Read_00_t), .en(Line4_Enable), .Q(L4_Banco00), .clk(Clock), .clr(Reset));
  Multiplexer #(.select(2), .width(32), .enable("false")) multiplexer_8 (
    .in0(Selected_BankL1), .in1(Selected_BankL2), .in2(Selected_BankL3), .in3(Selected_BankL4),
    .out(Cache_Data), .sel(Mem_Adress[5:4]));
  not not_3 (not_3_out, Cache_Hit_t);
  and and_3 (Ram_Read, Read, not_3_out);
  Register #(.width(32)) u_L1_Banco01 (.D(Read_01_t), .en(Line1_Enable), .Q(L1_Banco01), .clk(Clock), .clr(Reset));
  Register #(.width(32)) u_L2_Banco01 (.D(Read_01_t), .en(Line2_Enable), .Q(L2_Banco01), .clk(Clock), .clr(Reset));
  Register #(.width(32)) u_L3_Banco01 (.D(Read_01_t), .en(Line3_Enable), .Q(L3_Banco01), .clk(Clock), .clr(Reset));
  Register #(.width(32)) u_L4_Banco01 (.D(Read_01_t), .en(Line4_Enable), .Q(L4_Banco01), .clk(Clock), .clr(Reset));
  Multiplexer #(.select(2), .width(32), .enable("false")) multiplexer_9 (
    .in0(L2_Banco00), .in1(L2_Banco01), .in2(L2_Banco02), .in3(L2_Banco03), .out(Selected_BankL2),
    .sel(Mem_Adress[3:2]));
  Multiplexer #(.select(2), .width(32), .enable("false")) multiplexer_10 (
    .in0(L4_Banco00), .in1(L4_Banco01), .in2(L4_Banco02), .in3(L4_Banco03), .out(Selected_BankL4),
    .sel(Mem_Adress[3:2]));
  and and_4 (Cache_Hit_t, Tags_Same, Selected_Tag_Valid[14]);
  Register #(.width(32)) u_L1_Banco02 (.D(Read_02_t), .en(Line1_Enable), .Q(L1_Banco02), .clk(Clock), .clr(Reset));
  Register #(.width(32)) u_L2_Banco02 (.D(Read_02_t), .en(Line2_Enable), .Q(L2_Banco02), .clk(Clock), .clr(Reset));
  Register #(.width(32)) u_L3_Banco02 (.D(Read_02_t), .en(Line3_Enable), .Q(L3_Banco02), .clk(Clock), .clr(Reset));
  Register #(.width(32)) u_L4_Banco02 (.D(Read_02_t), .en(Line4_Enable), .Q(L4_Banco02), .clk(Clock), .clr(Reset));
  Comparator #(.width(14)) comparator_1 (
    .a(Selected_Tag_Valid[13:0]), .b(Mem_Adress[19:6]), .eq(Tags_Same));  // open: gt, lt
  D_Flip_Flop d_ff_1 (.clk(Clock), .D(Line4_Enable), .Q(_3_enable), .reset(Reset));  // open: Qn, preset, en
  Comparator #(.width(2)) comparator_2 (.a(Mem_Adress[3:2]), .b(2'b00), .eq(bank0));  // open: gt, lt
  Comparator #(.width(2)) comparator_3 (.a(Mem_Adress[3:2]), .b(2'b01), .eq(bank1));  // open: gt, lt
  Comparator #(.width(2)) comparator_4 (.a(Mem_Adress[3:2]), .b(2'b10), .eq(bank2));  // open: gt, lt
  Comparator #(.width(2)) comparator_5 (.a(Mem_Adress[3:2]), .b(2'b11), .eq(bank3));  // open: gt, lt
  D_Flip_Flop d_ff_2 (.clk(Clock), .D(Line2_Enable), .Q(_1_enable), .reset(Reset));  // open: Qn, preset, en
  Register #(.width(32)) u_L1_Banco03 (.D(Read_03_t), .en(Line1_Enable), .Q(L1_Banco03), .clk(Clock), .clr(Reset));
  Register #(.width(32)) u_L2_Banco03 (.D(Read_03_t), .en(Line2_Enable), .Q(L2_Banco03), .clk(Clock), .clr(Reset));
  Register #(.width(32)) u_L3_Banco03 (.D(Read_03_t), .en(Line3_Enable), .Q(L3_Banco03), .clk(Clock), .clr(Reset));
  Register #(.width(32)) u_L4_Banco03 (.D(Read_03_t), .en(Line4_Enable), .Q(L4_Banco03), .clk(Clock), .clr(Reset));
  D_Flip_Flop d_ff_3 (.clk(Clock), .D(Line1_Enable), .Q(_0_enable), .reset(Reset));  // open: Qn, preset, en
  D_Flip_Flop d_ff_4 (.clk(Clock), .D(Line3_Enable), .Q(_2_enable), .reset(Reset));  // open: Qn, preset, en
  and and_5 (and_5_out, Write, _0_enable);
  and and_6 (and_6_out, and_5_out, bank0);
  and and_7 (and_7_out, Write, _0_enable);
  and and_8 (and_8_out, and_7_out, bank1);
  and and_9 (and_9_out, Write, _0_enable);
  and and_10 (and_10_out, and_9_out, bank2);
  and and_11 (and_11_out, Write, _0_enable);
  and and_12 (and_12_out, and_11_out, bank3);
  and and_13 (and_13_out, Write, _2_enable);
  and and_14 (and_14_out, and_13_out, bank0);
  and and_15 (and_15_out, Write, _2_enable);
  and and_16 (and_16_out, and_15_out, bank1);
  and and_17 (and_17_out, Write, _2_enable);
  and and_18 (and_18_out, and_17_out, bank2);
  and and_19 (and_19_out, Write, _2_enable);
  and and_20 (and_20_out, and_19_out, bank3);
  and and_21 (E00, and_6_out, Cache_Hit_t);
  and and_22 (E01, and_8_out, Cache_Hit_t);
  and and_23 (E02, and_10_out, Cache_Hit_t);
  and and_24 (E03, and_12_out, Cache_Hit_t);
  and and_25 (E20, and_14_out, Cache_Hit_t);
  and and_26 (E21, and_16_out, Cache_Hit_t);
  and and_27 (E22, and_18_out, Cache_Hit_t);
  and and_28 (E23, and_20_out, Cache_Hit_t);
  and and_29 (and_29_out, Write, _1_enable);
  and and_30 (and_30_out, and_29_out, bank0);
  and and_31 (and_31_out, Write, _1_enable);
  and and_32 (and_32_out, and_31_out, bank1);
  and and_33 (and_33_out, Write, _1_enable);
  and and_34 (and_34_out, and_33_out, bank2);
  and and_35 (and_35_out, Write, _1_enable);
  and and_36 (and_36_out, and_35_out, bank3);
  and and_37 (and_37_out, Write, _3_enable);
  and and_38 (and_38_out, Write, _3_enable);
  and and_39 (and_39_out, Write, _3_enable);
  and and_40 (and_40_out, Write, _3_enable);
  and and_41 (E10, and_30_out, Cache_Hit_t);
  and and_42 (E11, and_32_out, Cache_Hit_t);
  and and_43 (E12, and_34_out, Cache_Hit_t);
  and and_44 (E13, and_36_out, Cache_Hit_t);
  and and_45 (and_45_out, and_37_out, bank0);
  and and_46 (E30, and_45_out, Cache_Hit_t);
  and and_47 (and_47_out, and_38_out, bank1);
  and and_48 (E31, and_47_out, Cache_Hit_t);
  and and_49 (and_49_out, and_39_out, bank2);
  and and_50 (E32, and_49_out, Cache_Hit_t);
  and and_51 (and_51_out, and_40_out, bank3);
  and and_52 (E33, and_51_out, Cache_Hit_t);
  and and_53 (Cache_Hit, Cache_Hit_t, Read);
  Register #(.width(32)) register_1 (.D(WriteData), .en(Write), .Q(Write_ram), .clk(Clock), .clr(Reset));

  // Other names for the same wires on the sheet: Tag[13:0] = Mem_Adress[19:6]; Index[1:0] = Mem_Adress[5:4];
  //   Read_Enable = Read; Valid = Selected_Tag_Valid[14]; Stored_Tag[13:0] = Selected_Tag_Valid[13:0];
  //   Word[1:0] = Mem_Adress[3:2]; Register_Input[31:0] = WriteData; Write_Data[31:0] = WriteData; Ram_Write = Write;
  //   Write_Enable = Write
endmodule

module Cache_2 (
  input  Clock,
  input  Reset,
  input  Read,
  input  Write,
  input  E_Cache,
  input  [31:0] Mem_Adress,
  input  [31:0] WriteData,
  input  [31:0] Read_00,
  input  [31:0] Read_01,
  input  [31:0] Read_02,
  input  [31:0] Read_03,
  output Cache_Hit,
  output [31:0] Write_ram,
  output [31:0] Cache_Data
);

  wire _0_enable, _1_enable, _2_enable, _3_enable, and_2_out, and_5_out, and_6_out, and_7_out, and_8_out,
       and_9_out, and_10_out, and_11_out, and_12_out, and_13_out, and_14_out, and_15_out, and_16_out,
       and_17_out, and_18_out, and_19_out, and_20_out, and_29_out, and_30_out, and_31_out, and_32_out,
       and_33_out, and_34_out, and_35_out, and_36_out, and_37_out, and_38_out, and_39_out, and_40_out,
       and_45_out, and_47_out, and_49_out, and_51_out, bank0, bank1, bank2, bank3, Cache_Hit_t, Cache_in,
       E00, E01, E02, E03, E10, E11, E12, E13, E20, E21, E22, E23, E30, E31, E32, E33, Line1_Enable,
       Line2_Enable, Line3_Enable, Line4_Enable, Line_Enable, not_1_out, not_2_out, Ram_Read, Tags_Same;
  wire [14:0] Selected_Tag_Valid, V_Tag1, V_Tag2, V_Tag3, V_Tag4;
  wire [31:0] L1_Banco00, L1_Banco01, L1_Banco02, L1_Banco03, L2_Banco00, L2_Banco01, L2_Banco02, L2_Banco03,
       L3_Banco00, L3_Banco01, L3_Banco02, L3_Banco03, L4_Banco00, L4_Banco01, L4_Banco02, L4_Banco03,
       Selected_BankL1, Selected_BankL2, Selected_BankL3, Selected_BankL4;

  Multiplexer #(.select(2), .width(15), .enable("false")) multiplexer_1 (
    .in0(V_Tag1), .in1(V_Tag2), .in2(V_Tag3), .in3(V_Tag4), .out(Selected_Tag_Valid), .sel(Mem_Adress[5:4]));
  or or_1 (Cache_in, Read, Write);
  and and_1 (Line_Enable, Write, not_1_out);
  not not_1 (not_1_out, Cache_Hit_t);
  and and_2 (and_2_out, Line_Enable, E_Cache);
  Demultiplexer #(.select(2), .enable("false")) demultiplexer_1 (
    .out0(Line1_Enable), .out1(Line2_Enable), .out2(Line3_Enable), .out3(Line4_Enable), .in(and_2_out),
    .sel(Mem_Adress[5:4]));
  Register #(.width(15)) u_V_Tag1 (
    .D({1'b1, Mem_Adress[19:6]}), .en(Line1_Enable), .Q(V_Tag1), .clk(Clock), .clr(Reset));
  Register #(.width(15)) u_V_Tag2 (
    .D({1'b1, Mem_Adress[19:6]}), .en(Line2_Enable), .Q(V_Tag2), .clk(Clock), .clr(Reset));
  Register #(.width(15)) V_Tag2_2 (
    .D({1'b1, Mem_Adress[19:6]}), .en(Line3_Enable), .Q(V_Tag3), .clk(Clock), .clr(Reset));
  Register #(.width(15)) u_V_Tag4 (
    .D({1'b1, Mem_Adress[19:6]}), .en(Line4_Enable), .Q(V_Tag4), .clk(Clock), .clr(Reset));
  Multiplexer #(.select(2), .width(32), .enable("false")) multiplexer_2 (
    .in0(L1_Banco00), .in1(L1_Banco01), .in2(L1_Banco02), .in3(L1_Banco03), .out(Selected_BankL1),
    .sel(Mem_Adress[3:2]));
  Multiplexer #(.select(2), .width(32), .enable("false")) multiplexer_3 (
    .in0(L3_Banco00), .in1(L3_Banco01), .in2(L3_Banco02), .in3(L3_Banco03), .out(Selected_BankL3),
    .sel(Mem_Adress[3:2]));
  Register #(.width(32)) u_L1_Banco00 (.D(Read_00), .en(Line1_Enable), .Q(L1_Banco00), .clk(Clock), .clr(Reset));
  Register #(.width(32)) u_L2_Banco00 (.D(Read_00), .en(Line2_Enable), .Q(L2_Banco00), .clk(Clock), .clr(Reset));
  Register #(.width(32)) u_L3_Banco00 (.D(Read_00), .en(Line3_Enable), .Q(L3_Banco00), .clk(Clock), .clr(Reset));
  Register #(.width(32)) u_L4_Banco00 (.D(Read_00), .en(Line4_Enable), .Q(L4_Banco00), .clk(Clock), .clr(Reset));
  Multiplexer #(.select(2), .width(32), .enable("false")) multiplexer_4 (
    .in0(Selected_BankL1), .in1(Selected_BankL2), .in2(Selected_BankL3), .in3(Selected_BankL4),
    .out(Cache_Data), .sel(Mem_Adress[5:4]));
  not not_2 (not_2_out, Cache_Hit_t);
  Register #(.width(32)) u_L1_Banco01 (.D(Read_01), .en(Line1_Enable), .Q(L1_Banco01), .clk(Clock), .clr(Reset));
  Register #(.width(32)) u_L2_Banco01 (.D(Read_01), .en(Line2_Enable), .Q(L2_Banco01), .clk(Clock), .clr(Reset));
  Register #(.width(32)) u_L3_Banco01 (.D(Read_01), .en(Line3_Enable), .Q(L3_Banco01), .clk(Clock), .clr(Reset));
  Register #(.width(32)) u_L4_Banco01 (.D(Read_01), .en(Line4_Enable), .Q(L4_Banco01), .clk(Clock), .clr(Reset));
  and and_3 (Ram_Read, Read, not_2_out);
  Multiplexer #(.select(2), .width(32), .enable("false")) multiplexer_5 (
    .in0(L2_Banco00), .in1(L2_Banco01), .in2(L2_Banco02), .in3(L2_Banco03), .out(Selected_BankL2),
    .sel(Mem_Adress[3:2]));
  Multiplexer #(.select(2), .width(32), .enable("false")) multiplexer_6 (
    .in0(L4_Banco00), .in1(L4_Banco01), .in2(L4_Banco02), .in3(L4_Banco03), .out(Selected_BankL4),
    .sel(Mem_Adress[3:2]));
  and and_4 (Cache_Hit_t, Tags_Same, Selected_Tag_Valid[14]);
  Register #(.width(32)) u_L1_Banco02 (.D(Read_02), .en(Line1_Enable), .Q(L1_Banco02), .clk(Clock), .clr(Reset));
  Register #(.width(32)) u_L2_Banco02 (.D(Read_02), .en(Line2_Enable), .Q(L2_Banco02), .clk(Clock), .clr(Reset));
  Register #(.width(32)) u_L3_Banco02 (.D(Read_02), .en(Line3_Enable), .Q(L3_Banco02), .clk(Clock), .clr(Reset));
  Register #(.width(32)) u_L4_Banco02 (.D(Read_02), .en(Line4_Enable), .Q(L4_Banco02), .clk(Clock), .clr(Reset));
  Comparator #(.width(14)) comparator_1 (
    .a(Selected_Tag_Valid[13:0]), .b(Mem_Adress[19:6]), .eq(Tags_Same));  // open: gt, lt
  Register #(.width(32)) u_L1_Banco03 (.D(Read_03), .en(Line1_Enable), .Q(L1_Banco03), .clk(Clock), .clr(Reset));
  Register #(.width(32)) u_L2_Banco03 (.D(Read_03), .en(Line2_Enable), .Q(L2_Banco03), .clk(Clock), .clr(Reset));
  Register #(.width(32)) u_L3_Banco03 (.D(Read_03), .en(Line3_Enable), .Q(L3_Banco03), .clk(Clock), .clr(Reset));
  Register #(.width(32)) u_L4_Banco03 (.D(Read_03), .en(Line4_Enable), .Q(L4_Banco03), .clk(Clock), .clr(Reset));
  Comparator #(.width(2)) comparator_2 (.a(Mem_Adress[3:2]), .b(2'b00), .eq(bank0));  // open: gt, lt
  Comparator #(.width(2)) comparator_3 (.a(Mem_Adress[3:2]), .b(2'b01), .eq(bank1));  // open: gt, lt
  Comparator #(.width(2)) comparator_4 (.a(Mem_Adress[3:2]), .b(2'b10), .eq(bank2));  // open: gt, lt
  Comparator #(.width(2)) comparator_5 (.a(Mem_Adress[3:2]), .b(2'b11), .eq(bank3));  // open: gt, lt
  D_Flip_Flop d_ff_1 (.clk(Clock), .D(Line2_Enable), .Q(_1_enable), .reset(Reset));  // open: Qn, preset, en
  D_Flip_Flop d_ff_2 (.clk(Clock), .D(Line1_Enable), .Q(_0_enable), .reset(Reset));  // open: Qn, preset, en
  D_Flip_Flop d_ff_3 (.clk(Clock), .D(Line3_Enable), .Q(_2_enable), .reset(Reset));  // open: Qn, preset, en
  D_Flip_Flop d_ff_4 (.clk(Clock), .D(Line4_Enable), .Q(_3_enable), .reset(Reset));  // open: Qn, preset, en
  and and_5 (and_5_out, Write, _0_enable);
  and and_6 (and_6_out, and_5_out, bank0);
  and and_7 (and_7_out, Write, _0_enable);
  and and_8 (and_8_out, and_7_out, bank1);
  and and_9 (and_9_out, Write, _0_enable);
  and and_10 (and_10_out, and_9_out, bank2);
  and and_11 (and_11_out, Write, _0_enable);
  and and_12 (and_12_out, and_11_out, bank3);
  and and_13 (and_13_out, Write, _2_enable);
  and and_14 (and_14_out, and_13_out, bank0);
  and and_15 (and_15_out, Write, _2_enable);
  and and_16 (and_16_out, and_15_out, bank1);
  and and_17 (and_17_out, Write, _2_enable);
  and and_18 (and_18_out, and_17_out, bank2);
  and and_19 (and_19_out, Write, _2_enable);
  and and_20 (and_20_out, and_19_out, bank3);
  and and_21 (E00, and_6_out, Cache_Hit_t);
  and and_22 (E01, and_8_out, Cache_Hit_t);
  and and_23 (E02, and_10_out, Cache_Hit_t);
  and and_24 (E03, and_12_out, Cache_Hit_t);
  and and_25 (E20, and_14_out, Cache_Hit_t);
  and and_26 (E21, and_16_out, Cache_Hit_t);
  and and_27 (E22, and_18_out, Cache_Hit_t);
  and and_28 (E23, and_20_out, Cache_Hit_t);
  and and_29 (and_29_out, Write, _1_enable);
  and and_30 (and_30_out, and_29_out, bank0);
  and and_31 (and_31_out, Write, _1_enable);
  and and_32 (and_32_out, and_31_out, bank1);
  and and_33 (and_33_out, Write, _1_enable);
  and and_34 (and_34_out, and_33_out, bank2);
  and and_35 (and_35_out, Write, _1_enable);
  and and_36 (and_36_out, and_35_out, bank3);
  and and_37 (and_37_out, Write, _3_enable);
  and and_38 (and_38_out, Write, _3_enable);
  and and_39 (and_39_out, Write, _3_enable);
  and and_40 (and_40_out, Write, _3_enable);
  and and_41 (E10, and_30_out, Cache_Hit_t);
  and and_42 (E11, and_32_out, Cache_Hit_t);
  and and_43 (E12, and_34_out, Cache_Hit_t);
  and and_44 (E13, and_36_out, Cache_Hit_t);
  and and_45 (and_45_out, and_37_out, bank0);
  and and_46 (E30, and_45_out, Cache_Hit_t);
  and and_47 (and_47_out, and_38_out, bank1);
  and and_48 (E31, and_47_out, Cache_Hit_t);
  and and_49 (and_49_out, and_39_out, bank2);
  and and_50 (E32, and_49_out, Cache_Hit_t);
  and and_51 (and_51_out, and_40_out, bank3);
  and and_52 (E33, and_51_out, Cache_Hit_t);
  and and_53 (Cache_Hit, Cache_Hit_t, Read);
  Register #(.width(32)) register_1 (.D(WriteData), .en(Write), .Q(Write_ram), .clk(Clock), .clr(Reset));

  // Other names for the same wires on the sheet: Tag[13:0] = Mem_Adress[19:6]; Index[1:0] = Mem_Adress[5:4];
  //   Read_Enable = Read; Valid = Selected_Tag_Valid[14]; Stored_Tag[13:0] = Selected_Tag_Valid[13:0];
  //   Word[1:0] = Mem_Adress[3:2]; Register_Input[31:0] = WriteData; Write_Data[31:0] = WriteData; Ram_Write = Write;
  //   Write_Enable = Write
endmodule

module Read_Ram_2 (
  input  [31:0] _00,
  input  [31:0] _01,
  input  [31:0] _02,
  input  [31:0] Mem_Ram_Adress,
  input  [31:0] _03,
  output [31:0] Read_Data,
  output [31:0] Read_00,
  output [31:0] Read_01,
  output [31:0] Read_02,
  output [31:0] Read_03
);

  wire [31:0] multiplexer_1_out;

  Multiplexer #(.select(2), .width(32)) multiplexer_1 (
    .in0(_00), .in1(_01), .in2(_02), .in3(_03), .out(multiplexer_1_out), .sel(Mem_Ram_Adress[3:2]));  // open: en
  Little_Endian little_endian_1 (.in_1(multiplexer_1_out), .out_2(Read_Data));
  Little_Endian little_endian_2 (.in_1(_00), .out_2(Read_00));
  Little_Endian little_endian_3 (.in_1(_01), .out_2(Read_01));
  Little_Endian little_endian_4 (.in_1(_02), .out_2(Read_02));
  Little_Endian little_endian_5 (.in_1(_03), .out_2(Read_03));

  // Other names for the same wires on the sheet: Bank0[31:0] = _00; Bank1[31:0] = _01; Bank2[31:0] = _02;
  //   Bank3[31:0] = _03; Low_mem[1:0] = Mem_Ram_Adress[3:2]
endmodule
